# Fritzing sketch ALU (saved by Fritzing 0.8.7b)
breadboards: 1

parts:
  IC1 = IC, DIP package, 14 pins [chip_label=74LS86]
  IC2 = IC, DIP package, 16 pins [chip_label=74LS283]
  IC3 = DIP - 20 pins [chip_label=74LS245 package="DIP (Dual Inline) [THT]"]
  IC4 = IC, DIP package, 14 pins [chip_label=74LS86]
  IC5 = IC, DIP package, 16 pins [chip_label=74LS283]

nets:
  SUB: IC1.pin1, IC1.pin4, IC1.pin9, IC1.pin12, IC2.pin7, IC4.pin1, IC4.pin4, IC4.pin9, IC4.pin12
  FROM REG B 4: IC1.pin2
  N1: IC1.pin3, IC5.pin6
  FROM REG B 5: IC1.pin5
  N2: IC1.pin6, IC5.pin2
  GND: IC1.pin7, IC2.pin8, IC3.GND, IC4.pin7, IC5.pin8, IC5.pin9
  N3: IC1.pin8, IC5.pin15
  FROM REG B 6: IC1.pin10
  N4: IC1.pin11, IC5.pin11
  FROM REG B 7: IC1.pin13
  5V: IC1.pin14, IC2.pin16, IC3.DIR, IC3.VCC, IC4.pin14, IC5.pin16
  N5: IC2.pin1, IC3.A2
  N6: IC2.pin2, IC4.pin6
  FROM REG A 1: IC2.pin3
  N7: IC2.pin4, IC3.A1
  FROM REG A 0: IC2.pin5
  N8: IC2.pin6, IC4.pin3
  N9: IC2.pin9, IC5.pin7
  N10: IC2.pin10, IC3.A4
  N11: IC2.pin11, IC4.pin11
  FROM REG A 3: IC2.pin12
  N12: IC2.pin13, IC3.A3
  FROM REG A 2: IC2.pin14
  N13: IC2.pin15, IC4.pin8
  N14: IC3.A5, IC5.pin4
  N15: IC3.A6, IC5.pin1
  N16: IC3.A7, IC5.pin13
  N17: IC3.A8, IC5.pin10
  TO BUS 7: IC3.B8
  TO BUS 6: IC3.B7
  TO BUS 5: IC3.B6
  TO BUS 4: IC3.B5
  TO BUS 3: IC3.B4
  TO BUS 2: IC3.B3
  TO BUS 1: IC3.B2
  TO BUS 0: IC3.B1
  SUM OUT: IC3.~OE
  FROM REG B 0: IC4.pin2
  FROM REG B 1: IC4.pin5
  FROM REG B 2: IC4.pin10
  FROM REG B 3: IC4.pin13
  FROM REG A 5: IC5.pin3
  FROM REG A 4: IC5.pin5
  FROM REG A 7: IC5.pin12
  FROM REG A 6: IC5.pin14

custom parts:
  DIP - 20 pins: A DIP stand-in part for whatever IC you want. With 20 pins on a 300mil dual inline package (DIP) footprint.
