# Fritzing sketch IR (saved by Fritzing 0.8.7b)
breadboards: 1

parts:
  IC7 = IC, DIP package, 20 pins [chip_label=74LS245]
  IC8 = IC, DIP package, 16 pins [chip_label=74LS173]
  IC9 = IC, DIP package, 16 pins [chip_label=74LS173]

nets:
  5V: IC7.pin1, IC7.pin20, IC8.pin16
  N1: IC7.pin2, IC9.pin3
  N2: IC7.pin3, IC9.pin4
  N3: IC7.pin4, IC9.pin5
  N4: IC7.pin5, IC9.pin6
  GND: IC7.pin6, IC7.pin7, IC7.pin8, IC7.pin9, IC7.pin10, IC8.pin1, IC8.pin2, IC8.pin8, IC9.pin1, IC9.pin2, IC9.pin8
  BUS7: IC7.pin11, IC8.pin11
  BUS6: IC7.pin12, IC8.pin12
  BUS5: IC7.pin13, IC8.pin13
  BUS4: IC7.pin14, IC8.pin14
  BUS3: IC7.pin15, IC9.pin11
  BUS2: IC7.pin16, IC9.pin12
  BUS1: IC7.pin17, IC9.pin13
  BUS0: IC7.pin18, IC9.pin14
  ~Enable: IC7.pin19
  EE_A3: IC8.pin3
  EE_A4: IC8.pin4
  EE_A5: IC8.pin5
  EE_A6: IC8.pin6
  Clock: IC8.pin7, IC9.pin7
  Data Enable: IC8.pin9, IC8.pin10, IC9.pin9, IC9.pin10
  Clear: IC8.pin15, IC9.pin15

notes:
  BUS OUTPUT/INPUT
  TO MICROCODE EEPROM ADDRESS LINES A3 - A6
