# Fritzing sketch Memory Address Register (saved by Fritzing 0.8.7b)
breadboards: 1

parts:
  IC6 = IC, DIP package, 16 pins [chip_label=74LS173]
  SW1 = DIP SWITCH [package=dipswitch-02]
  SW2 = DIP SWITCH [package=dipswitch-02]
  IC7 = IC, DIP package, 16 pins [chip_label=74LS157]
  S3 = Toggle Switch [package=THT]
  LED1 = LED - 5mm [color="Red (633nm)" package="5 mm [THT]"]
  LED2 = LED - 5mm [color="Red (633nm)" package="5 mm [THT]"]
  LED3 = LED - 5mm [color="Red (633nm)" package="5 mm [THT]"]
  LED4 = LED - 5mm [color="Red (633nm)" package="5 mm [THT]"]

nets:
  GND: IC6.pin1, IC6.pin2, IC6.pin8, IC6.pin15, SW1.1, SW1.2, SW2.1, SW2.2, IC7.pin2, IC7.pin5, IC7.pin8, IC7.pin11, IC7.pin14, IC7.pin15, S3.L2, LED1.cathode, LED2.cathode, LED3.cathode, LED4.cathode
  N1: IC6.pin3, IC7.pin3
  N2: IC6.pin4, IC7.pin6
  N3: IC6.pin5, IC7.pin13
  N4: IC6.pin6, IC7.pin10
  Clock: IC6.pin7
  DATA ENABLE: IC6.pin9, IC6.pin10
  FROM BUS3: IC6.pin11
  FROM BUS2: IC6.pin12
  FROM BUS1: IC6.pin13
  FROM BUS0: IC6.pin14
  5V: IC6.pin16, SW1.3, SW1.4, SW2.3, SW2.4, IC7.pin16, S3.L1
  N5: IC7.pin1, S3.COM
  TO RAM ADDRESS 0: IC7.pin4, LED1.anode
  TO RAM ADDRESS 1: IC7.pin7, LED4.anode
  TO RAM ADDRESS 3: IC7.pin9, LED2.anode
  TO RAM ADDRESS 2: IC7.pin12, LED3.anode
