# Fritzing sketch Microcode storage (saved by Fritzing 0.8.7b)
breadboards: 1

parts:
  IC2 = IC, DIP package, 24 pins [chip_label="EEPROM AT28C16"]
  IC3 = IC, DIP package, 24 pins [chip_label="EEPROM AT28C16"]

nets:
  GND: IC2.pin1, IC2.pin12, IC2.pin18, IC2.pin19, IC2.pin20, IC2.pin22, IC2.pin23, IC3.pin1, IC3.pin12, IC3.pin18, IC3.pin19, IC3.pin20, IC3.pin22, IC3.pin23
  FROM INSTRUCTION REGISTER 7: IC2.pin2, IC3.pin2
  FROM INSTRUCTION REGISTER 6: IC2.pin3, IC3.pin3
  FROM INSTRUCTION REGISTER 5: IC2.pin4, IC3.pin4
  FROM INSTRUCTION REGISTER 4: IC2.pin5, IC3.pin5
  FROM CYCLE COUNTER 2: IC2.pin6, IC3.pin6
  FROM CYCLE COUNTER 1: IC2.pin7, IC3.pin7
  FROM CYCLE COUNTER 0: IC2.pin8, IC3.pin8
  HALT: IC2.pin9
  MEMORY ADDRESS IN: IC2.pin10
  RAM OUT: IC2.pin11
  RAM IN: IC2.pin13
  INSTRUCTION REGISTER IN: IC2.pin14
  INSTRUCTION REGISTER OUT: IC2.pin15
  REGISTER A IN: IC2.pin16
  REGISTER A OUT: IC2.pin17
  5V: IC2.pin21, IC2.pin24, IC3.pin21, IC3.pin24
  SUB: IC3.pin9
  ALU OUT: IC3.pin10
  JUMP: IC3.pin11
  PROGRAM COUNTER OUT: IC3.pin13
  PROGRAM COUNTER ENABLE: IC3.pin14
  DISPLAY: IC3.pin15
  REGISTER B OUT: IC3.pin16
  REGISTER B IN: IC3.pin17
