# Fritzing sketch OUTPUT (saved by Fritzing 0.8.7b)
breadboards: 1

parts:
  7_Segment_4_Digit_Display1 = 7-SEGMENT-4DIGIT common anode [part_number="5461BS - 5462BS" package=7-segment-4digit-anode]
  IC1 = DIP - 24 pins [chip_label="EEPROM AT28C16" package="DIP (Dual Inline) [THT]"]
  IC2 = IC, DIP package, 16 pins [chip_label=74LS139]
  IC3 = IC, DIP package, 16 pins [chip_label=74LS76]
  IC4 = IC, DIP package, 20 pins [chip_label=74LS273]
  IC5 = IC, DIP package, 14 pins [chip_label=74LS08]
  IC6 = IC, DIP package, 8 pins [chip_label="555 Timer"]
  C1 = Ceramic Capacitor [capacitance=10nF package="100 mil [THT, multilayer]"]
  R1 = Resistor [tolerance=±5% resistance=2.2k package=THT]
  R2 = Resistor [tolerance=±5% resistance=100k package=THT]
  C2 = Ceramic Capacitor [capacitance=10nF package="100 mil [THT, multilayer]"]

nets:
  N1: 7_Segment_4_Digit_Display1.pin_1, IC1.I/O_2
  N2: 7_Segment_4_Digit_Display1.pin_2, IC1.I/O_3
  N3: 7_Segment_4_Digit_Display1.pin_3, IC1.I/O_7
  N4: 7_Segment_4_Digit_Display1.pin_4, IC1.I/O_4
  N5: 7_Segment_4_Digit_Display1.pin_5, IC1.I/O_0
  N6: 7_Segment_4_Digit_Display1.pin_6, IC2.pin12
  N7: 7_Segment_4_Digit_Display1.pin_7, IC1.I/O_5
  N8: 7_Segment_4_Digit_Display1.pin_8, IC2.pin11
  N9: 7_Segment_4_Digit_Display1.pin_9, IC2.pin10
  N10: 7_Segment_4_Digit_Display1.pin_10, IC1.I/O_1
  N11: 7_Segment_4_Digit_Display1.pin_11, IC1.I/O_6
  N12: 7_Segment_4_Digit_Display1.pin_12, IC2.pin9
  N13: IC1.A7, IC4.pin19
  N14: IC1.A6, IC4.pin16
  N15: IC1.A5, IC4.pin15
  N16: IC1.A4, IC4.pin12
  N17: IC1.A3, IC4.pin9
  N18: IC1.A2, IC4.pin6
  N19: IC1.A1, IC4.pin5
  N20: IC1.A0, IC4.pin2
  GND: IC1.GND, IC1.~CE, IC1.~OE, IC2.pin8, IC2.pin15, IC3.pin13, IC4.pin10, IC5.pin7, IC6.pin1, C1.1, C2.0
  2's COMPLEMENT: IC1.A10
  5V: IC1.~WE, IC1.VCC, IC2.pin16, IC3.pin2, IC3.pin3, IC3.pin4, IC3.pin5, IC3.pin7, IC3.pin8, IC3.pin9, IC3.pin12, IC3.pin16, IC4.pin1, IC4.pin20, IC5.pin14, IC6.pin4, IC6.pin8, R1.Pin_1
  N21: IC1.A9, IC2.pin14, IC3.pin15
  N22: IC1.A8, IC2.pin13, IC3.pin1, IC3.pin11
  N23: IC3.pin6, IC6.pin3
  FROM BUS 0: IC4.pin3
  FROM BUS 1: IC4.pin4
  FROM BUS 2: IC4.pin7
  FROM BUS 3: IC4.pin8
  N24: IC4.pin11, IC5.pin11
  FROM BUS 4: IC4.pin13
  FROM BUS 5: IC4.pin14
  FROM BUS 6: IC4.pin17
  FROM BUS 7: IC4.pin18
  DISPLAY OUT CONTROL: IC5.pin12
  CLOCK: IC5.pin13
  N25: IC6.pin2, C1.0
  N26: IC6.pin5, C2.1
  N27: IC6.pin6, R2.Pin_1
  N28: IC6.pin7, R1.Pin_0, R2.Pin_0

custom parts:
  7-SEGMENT-4DIGIT common anode: A 7 Segment 4 Digit common anode display, with decimal points
  DIP - 24 pins: A DIP stand-in part for whatever IC you want. With 24 pins on a 300mil dual inline package (DIP) footprint.
