# Fritzing sketch Program Counter (saved by Fritzing 0.8.7b)
breadboards: 1

parts:
  IC1 = IC, DIP package, 16 pins [chip_label=74LS161]
  IC2 = DIP - 20 pins [chip_label=74LS245 package="DIP (Dual Inline) [THT]"]
  LED1 = LED - 5mm [color="Red (633nm)" package="5 mm [THT]"]
  LED2 = LED - 5mm [color="Red (633nm)" package="5 mm [THT]"]
  LED3 = LED - 5mm [color="Red (633nm)" package="5 mm [THT]"]
  LED4 = LED - 5mm [color="Red (633nm)" package="5 mm [THT]"]

nets:
  GND: IC1.pin1, IC1.pin8, IC2.DIR, IC2.GND, IC2.B4, IC2.B3, IC2.B2, IC2.B1, LED1.cathode, LED2.cathode, LED3.cathode, LED4.cathode
  CLOCK: IC1.pin2
  FROM BUS 3: IC1.pin3, IC2.A5
  FROM BUS 2: IC1.pin4, IC2.A6
  FROM BUS 1: IC1.pin5, IC2.A7
  FROM BUS 0: IC1.pin6, IC2.A8
  PROGRAM COUNTER ENABLE: IC1.pin7, IC1.pin10
  JUMP: IC1.pin9
  TO BUS 0: IC1.pin11, IC2.B8, LED1.anode
  TO BUS 1: IC1.pin12, IC2.B7, LED2.anode
  TO BUS 2: IC1.pin13, IC2.B6, LED3.anode
  TO BUS 3: IC1.pin14, IC2.B5, LED4.anode
  5V: IC1.pin16, IC2.VCC
  PROGRAM COUNTER OUT: IC2.~OE

custom parts:
  DIP - 20 pins: A DIP stand-in part for whatever IC you want. With 20 pins on a 300mil dual inline package (DIP) footprint.
