# Fritzing sketch RAM DATA INPUT CIRCUIT (saved by Fritzing 0.8.7b)
breadboards: 1

parts:
  SW1 = DIP Switch 8 Position [package=dipswitch-08]
  R1 = Resistor [tolerance=±5% resistance=1k package=THT]
  C1 = Ceramic Capacitor [capacitance=10nF package="100 mil [THT, multilayer]"]
  S1 = Pushbutton [package="[THT]"]
  S2 = Toggle Switch [package=THT]
  74ls157_(LSB) = IC, DIP package, 16 pins [chip_label=74LS157]
  74ls157_(MSB) = IC, DIP package, 16 pins [chip_label=74LS157]
  74ls157_(selector = IC, DIP package, 16 pins [chip_label=74LS157]
  74ls00 = IC, DIP package, 14 pins [chip_label=74LS00]

nets (from the schematic view):
  GND: SW1.1, SW1.2, SW1.3, SW1.4, SW1.5, SW1.6, SW1.7, SW1.8, R1.Pin_0, S1.Pin_1, S1.Pin_2, S2.L2, 74ls157_(LSB).pin2, 74ls157_(LSB).pin5, 74ls157_(LSB).pin8, 74ls157_(LSB).pin11, 74ls157_(LSB).pin14, 74ls157_(LSB).pin15, 74ls157_(MSB).pin2, 74ls157_(MSB).pin5, 74ls157_(MSB).pin8, 74ls157_(MSB).pin11, 74ls157_(MSB).pin14, 74ls157_(MSB).pin15, 74ls157_(selector.pin8, 74ls157_(selector.pin15, 74ls00.pin7, 74ls00.pin13
  5V: SW1.9, SW1.10, SW1.11, SW1.12, SW1.13, SW1.14, SW1.15, SW1.16, S1.Pin_3, S1.Pin_4, S2.L1, 74ls157_(LSB).pin16, 74ls157_(MSB).pin16, 74ls157_(selector.pin16, 74ls00.pin14
  N1: R1.Pin_1, C1.1, 74ls00.pin1
  clock: C1.0
  N2: S2.COM, 74ls157_(LSB).pin1, 74ls157_(MSB).pin1, 74ls157_(selector.pin1
  From BUS0: 74ls157_(LSB).pin3
  TO RAM0: 74ls157_(LSB).pin4
  From BUS1: 74ls157_(LSB).pin6
  TO RAM1: 74ls157_(LSB).pin7
  TO RAM3: 74ls157_(LSB).pin9
  From BUS3: 74ls157_(LSB).pin10
  TO RAM2: 74ls157_(LSB).pin12
  From BUS2: 74ls157_(LSB).pin13
  From BUS4: 74ls157_(MSB).pin3
  TO RAM4: 74ls157_(MSB).pin4
  From BUS5: 74ls157_(MSB).pin6
  TO RAM5: 74ls157_(MSB).pin7
  TO RAM7: 74ls157_(MSB).pin9
  From BUS7: 74ls157_(MSB).pin10
  TO RAM6: 74ls157_(MSB).pin12
  From BUS6: 74ls157_(MSB).pin13
  TO RAM WRITE ENABLE: 74ls157_(selector.pin12
  N3: 74ls157_(selector.pin13, 74ls00.pin3
  RAM IN: 74ls00.pin2

notes:
  SELECT
