# Fritzing sketch RAM (saved by Fritzing 0.8.7b)
breadboards: 1

parts:
  IC2 = IC, DIP package, 16 pins [chip_label=74LS189]
  IC4 = IC, DIP package, 16 pins [chip_label=74LS189]
  IC5 = IC, DIP package, 14 pins [chip_label=74LS04]
  IC6 = IC, DIP package, 14 pins [chip_label=74LS04]
  IC7 = IC, DIP package, 20 pins [chip_label=74LS245]

nets:
  FROM DIPSW/BUS 0: IC2.pin1, IC4.pin1, IC4.pin4
  GND: IC2.pin2, IC2.pin8, IC4.pin2, IC4.pin8, IC5.pin7, IC6.pin7, IC7.pin10
  FROM BUTTON/CONTROL: IC2.pin3, IC4.pin3
  FROM DIPSW/BUS 4: IC2.pin4
  N1: IC2.pin5, IC5.pin11
  FROM DIPSW/BUS 5: IC2.pin6
  N2: IC2.pin7, IC5.pin13
  N3: IC2.pin9, IC6.pin3
  FROM DIPSW/BUS 7: IC2.pin10
  N4: IC2.pin11, IC6.pin1
  FROM DIPSW/BUS 6: IC2.pin12
  FROM DIPSW/BUS 3: IC2.pin13, IC4.pin10, IC4.pin13
  FROM DIPSW/BUS 2: IC2.pin14, IC4.pin12, IC4.pin14
  FROM DIPSW/BUS 1: IC2.pin15, IC4.pin6, IC4.pin15
  5V: IC2.pin16, IC4.pin16, IC5.pin14, IC6.pin14, IC7.pin1, IC7.pin20
  N5: IC4.pin5, IC5.pin1
  N6: IC4.pin7, IC5.pin3
  N7: IC4.pin9, IC5.pin5
  N8: IC4.pin11, IC5.pin9
  N9: IC5.pin2, IC7.pin2
  N10: IC5.pin4, IC7.pin3
  N11: IC5.pin6, IC7.pin4
  N12: IC5.pin8, IC7.pin5
  N13: IC5.pin10, IC7.pin6
  N14: IC5.pin12, IC7.pin7
  N15: IC6.pin2, IC7.pin8
  N16: IC6.pin4, IC7.pin9
  TO BUS 7: IC7.pin11
  TO BUS 6: IC7.pin12
  TO BUS 5: IC7.pin13
  TO BUS 4: IC7.pin14
  TO BUS 3: IC7.pin15
  TO BUS 2: IC7.pin16
  TO BUS 1: IC7.pin17
  TO BUS 0: IC7.pin18
  RAM OUT: IC7.pin19
