# Fritzing sketch RegisterA_B (saved by Fritzing 0.8.7b)
breadboards: 1

parts:
  IC4 = IC, DIP package, 20 pins [chip_label=74LS245]
  IC5 = IC, DIP package, 16 pins [chip_label=74LS173]
  IC6 = IC, DIP package, 16 pins [chip_label=74LS173]

nets:
  5V: IC4.pin1, IC4.pin20, IC5.pin16, IC6.pin16
  ALU0: IC4.pin2, IC6.pin3
  ALU1: IC4.pin3, IC6.pin4
  ALU2: IC4.pin4, IC6.pin5
  ALU3: IC4.pin5, IC6.pin6
  ALU4: IC4.pin6, IC5.pin3
  ALU5: IC4.pin7, IC5.pin4
  ALU6: IC4.pin8, IC5.pin5
  ALU7: IC4.pin9, IC5.pin6
  GND: IC4.pin10, IC5.pin1, IC5.pin2, IC5.pin8, IC6.pin1, IC6.pin2, IC6.pin8
  BUS7: IC4.pin11, IC5.pin11
  BUS6: IC4.pin12, IC5.pin12
  BUS5: IC4.pin13, IC5.pin13
  BUS4: IC4.pin14, IC5.pin14
  BUS3: IC4.pin15, IC6.pin11
  BUS2: IC4.pin16, IC6.pin12
  BUS1: IC4.pin17, IC6.pin13
  BUS0: IC4.pin18, IC6.pin14
  ~Enable: IC4.pin19
  Clock: IC5.pin7, IC6.pin7
  Data Enable: IC5.pin9, IC5.pin10, IC6.pin9, IC6.pin10
  Clear: IC5.pin15, IC6.pin15

notes:
  OUTPUT/INPUT FROM BUS
  TO ARITHMETIC LOGIC UNIT
